# Fritzing sketch almabraxas-2-10 (saved by Fritzing 0.9.3b)
circuit board: 20cm x 10cm
breadboards: 1

parts:
  GPS = Adafruit Ultimate GPS Breakout
  microSD1 = MicroSD Breakout
  D1 = Rectifier Diode [part_number=1N4001 package="300 mil [THT]"]
  C6 = Capacitor [package=cap-pth-small2]
  VCC1 = Battery block 9V
  C8 = Capacitor Polarized [package=cpol-radial-100uf-25v]
  R78 = Recom R785.0-1.0 [package="TO220 [THT]"]
  R79 = Resistor [tolerance=±5% resistance=2.2k package=THT]
  R80 = Resistor [tolerance=±5% resistance=4.7k package=THT]
  Teensy_3_1 = Teensy 3.1
  C9 = Capacitor [package=cap-pth-small2]
  C10 = Capacitor [package=cap-pth-small2]
  C11 = Capacitor [package=cap-pth-small2]
  RB1 = RB1 connector [form="♀ (female)" package=THT]
  J1 = female pin header, 2 pins [form="♀ (female)"]  # not connected

nets:
  N1: GPS.TX, Teensy_3_1.D0
  N2: GPS.RX, Teensy_3_1.D1
  GND: GPS.GND, microSD1.GND, C6.1, VCC1.-, C8.-, R78.GND, R79.Pin_1, Teensy_3_1.GND, C9.2, C11.1, RB1.CTS, RB1.RTS, RB1.GND
  VIN: GPS.VIN, microSD1.5V, D1.anode, C6.2, C8.+, R78.+Vout, Teensy_3_1.Vin, C9.1, C11.2
  N3: microSD1.CS, Teensy_3_1.A1/D15
  N4: microSD1.DI, Teensy_3_1.D11
  N5: microSD1.DO, Teensy_3_1.D12
  N6: microSD1.CLK, Teensy_3_1.A0/D14
  N7: VCC1.+, R78.+Vin, R80.Pin_0
  N8: R79.Pin_0, R80.Pin_1
  N9: Teensy_3_1.D9, RB1.RX
  N10: Teensy_3_1.D10, RB1.TX
  N11: Teensy_3_1.3V3, C10.1

notes:
  VCC
  GND
  Power block
  Battery voltage sensor
  MCU
  pressure + temp sensor
  SCL
  SDA

custom parts:
  MicroSD Breakout: 5V-ready microSD Breakout with Level Shifter
  Recom R785.0-1.0: 5V DC switching Voltage Regulator 1A (input voltage 6.5-18V)
  RB1 connector: Connector for RockBlock 1 satellite modem
